// Logisim project ALU.circ as structural Verilog: 9 circuits, main circuit full adder
module full_adder (
  input  X,
  input  Y,
  input  Z,
  output sum,
  output C
);

  wire and_1_out, and_2_out, xor_1_out;

  xor xor_1 (xor_1_out, X, Y);
  and and_1 (and_1_out, X, Y);
  xor xor_2 (sum, xor_1_out, Z);
  and and_2 (and_2_out, xor_1_out, Z);
  or or_1 (C, and_2_out, and_1_out);
endmodule

module _4_bit_adder (
  input  B1,
  input  A1,
  input  B0,
  input  A0,
  input  B3,
  input  A3,
  input  B2,
  input  A2,
  output Carry,
  output sum3,
  output sum2,
  output sum1,
  output sum0
);

  wire full_adder_2_c, full_adder_3_c, full_adder_4_c;

  full_adder full_adder_1 (.X(full_adder_2_c), .Y(B3), .sum(sum3), .Z(A3), .C(Carry));
  full_adder full_adder_2 (.X(full_adder_3_c), .Y(B2), .sum(sum2), .Z(A2), .C(full_adder_2_c));
  full_adder full_adder_3 (.X(full_adder_4_c), .Y(B1), .sum(sum1), .Z(A1), .C(full_adder_3_c));
  full_adder full_adder_4 (.X(1'b0), .Y(B0), .sum(sum0), .Z(A0), .C(full_adder_4_c));
endmodule

module adder_subtractor (
  input  B3,
  input  B2,
  input  B1,
  input  B0,
  input  Selector,
  input  A3,
  input  A2,
  input  A1,
  input  A0,
  output Carry,
  output sum3,
  output sum2,
  output sum1,
  output sum0
);

  wire full_adder_2_c, full_adder_3_c, full_adder_4_c, xor_1_out, xor_2_out, xor_3_out, xor_4_out;

  xor xor_1 (xor_1_out, B3, Selector);
  full_adder full_adder_1 (.X(full_adder_2_c), .Y(xor_1_out), .sum(sum3), .Z(A3), .C(Carry));
  xor xor_2 (xor_2_out, B2, Selector);
  full_adder full_adder_2 (.X(full_adder_3_c), .Y(xor_2_out), .sum(sum2), .Z(A2), .C(full_adder_2_c));
  xor xor_3 (xor_3_out, B1, Selector);
  full_adder full_adder_3 (.X(full_adder_4_c), .Y(xor_3_out), .sum(sum1), .Z(A1), .C(full_adder_3_c));
  xor xor_4 (xor_4_out, B0, Selector);
  full_adder full_adder_4 (.X(Selector), .Y(xor_4_out), .sum(sum0), .Z(A0), .C(full_adder_4_c));
endmodule

module _4_bit_AND (
  input  A0,
  input  B0,
  input  A1,
  input  B1,
  input  A2,
  input  B2,
  input  A3,
  input  B3,
  output out_9,
  output out_10,
  output out_11,
  output out_12
);

  and and_1 (out_9, A0, B0);
  and and_2 (out_10, A1, B1);
  and and_3 (out_11, A2, B2);
  and and_4 (out_12, A3, B3);
endmodule

module _4_bit_OR (
  input  A0,
  input  B0,
  input  A1,
  input  B1,
  input  A2,
  input  B2,
  input  A3,
  input  B3,
  output out_9,
  output out_10,
  output out_11,
  output out_12
);

  or or_1 (out_9, A0, B0);
  or or_2 (out_10, A1, B1);
  or or_3 (out_11, A2, B2);
  or or_4 (out_12, A3, B3);
endmodule

module _4_bit_NOT (
  input  A0,
  input  A1,
  input  A2,
  input  A3,
  output out_5,
  output out_6,
  output out_7,
  output out_8
);

  not not_1 (out_5, A0);
  not not_2 (out_6, A1);
  not not_3 (out_7, A2);
  not not_4 (out_8, A3);
endmodule

module _4_bit_XOR (
  input  A0,
  input  B0,
  input  A1,
  input  B1,
  input  A2,
  input  B2,
  input  A3,
  input  B3,
  output out_9,
  output out_10,
  output out_11,
  output out_12
);

  xor xor_1 (out_9, A0, B0);
  xor xor_2 (out_10, A1, B1);
  xor xor_3 (out_11, A2, B2);
  xor xor_4 (out_12, A3, B3);
endmodule

module ALU (
  input  A0,
  input  A1,
  input  A2,
  input  A3,
  input  B0,
  input  B1,
  input  B2,
  input  B3,
  input  [2:0] Selector,
  output OUT0,
  output OUT1,
  output OUT2,
  output OUT3,
  output Carry
);

  wire adder_subtractor_1_carry, adder_subtractor_1_sum0, adder_subtractor_1_sum1, adder_subtractor_1_sum2,
       adder_subtractor_1_sum3, adder_subtractor_2_carry, adder_subtractor_2_sum0, adder_subtractor_2_sum1,
       adder_subtractor_2_sum2, adder_subtractor_2_sum3, n4_bit_adder_1_carry, n4_bit_adder_1_sum0,
       n4_bit_adder_1_sum1, n4_bit_adder_1_sum2, n4_bit_adder_1_sum3, n4_bit_adder_2_carry,
       n4_bit_adder_2_sum0, n4_bit_adder_2_sum1, n4_bit_adder_2_sum2, n4_bit_adder_2_sum3,
       n4_bit_and_1_out_9, n4_bit_and_1_out_10, n4_bit_and_1_out_11, n4_bit_and_1_out_12, n4_bit_not_1_out_5,
       n4_bit_not_1_out_6, n4_bit_not_1_out_7, n4_bit_not_1_out_8, n4_bit_or_1_out_9, n4_bit_or_1_out_10,
       n4_bit_or_1_out_11, n4_bit_or_1_out_12, n4_bit_xor_1_out_9, n4_bit_xor_1_out_10, n4_bit_xor_1_out_11,
       n4_bit_xor_1_out_12;

  _4_bit_adder u_4_bit_adder_1 (
    .Carry(n4_bit_adder_1_carry), .B3(B3), .A3(A3), .B2(B2), .A2(A2), .B1(B1), .A1(A1), .B0(B0), .A0(A0),
    .sum3(n4_bit_adder_1_sum3), .sum2(n4_bit_adder_1_sum2), .sum1(n4_bit_adder_1_sum1),
    .sum0(n4_bit_adder_1_sum0));
  adder_subtractor adder_subtractor_1 (
    .Carry(adder_subtractor_1_carry), .Selector(1'b1), .B3(B3), .A3(A3), .B2(B2), .A2(A2), .B1(B1), .A1(A1),
    .B0(B0), .A0(A0), .sum3(adder_subtractor_1_sum3), .sum2(adder_subtractor_1_sum2),
    .sum1(adder_subtractor_1_sum1), .sum0(adder_subtractor_1_sum0));
  adder_subtractor adder_subtractor_2 (
    .Carry(adder_subtractor_2_carry), .Selector(1'b1), .B3(1'b0), .A3(A3), .B2(1'b0), .A2(A2), .B1(1'b0),
    .A1(A1), .B0(1'b1), .A0(A0), .sum3(adder_subtractor_2_sum3), .sum2(adder_subtractor_2_sum2),
    .sum1(adder_subtractor_2_sum1), .sum0(adder_subtractor_2_sum0));
  _4_bit_adder u_4_bit_adder_2 (
    .Carry(n4_bit_adder_2_carry), .B3(1'b0), .A3(A3), .B2(1'b0), .A2(A2), .B1(1'b0), .A1(A1), .B0(1'b1),
    .A0(A0), .sum3(n4_bit_adder_2_sum3), .sum2(n4_bit_adder_2_sum2), .sum1(n4_bit_adder_2_sum1),
    .sum0(n4_bit_adder_2_sum0));
  _4_bit_AND u_4_bit_and_1 (
    .A0(A0), .B0(B0), .A1(A1), .B1(B1), .A2(A2), .B2(B2), .A3(A3), .B3(B3), .out_9(n4_bit_and_1_out_9),
    .out_10(n4_bit_and_1_out_10), .out_11(n4_bit_and_1_out_11), .out_12(n4_bit_and_1_out_12));
  _4_bit_OR u_4_bit_or_1 (
    .A0(A0), .B0(B0), .A1(A1), .B1(B1), .A2(A2), .B2(B2), .A3(A3), .B3(B3), .out_9(n4_bit_or_1_out_9),
    .out_10(n4_bit_or_1_out_10), .out_11(n4_bit_or_1_out_11), .out_12(n4_bit_or_1_out_12));
  _4_bit_NOT u_4_bit_not_1 (
    .A0(A0), .A1(A1), .A2(A2), .A3(A3), .out_5(n4_bit_not_1_out_5), .out_6(n4_bit_not_1_out_6),
    .out_7(n4_bit_not_1_out_7), .out_8(n4_bit_not_1_out_8));
  _4_bit_XOR u_4_bit_xor_1 (
    .A0(A0), .B0(B0), .A1(A1), .B1(B1), .A2(A2), .B2(B2), .A3(A3), .B3(B3), .out_9(n4_bit_xor_1_out_9),
    .out_10(n4_bit_xor_1_out_10), .out_11(n4_bit_xor_1_out_11), .out_12(n4_bit_xor_1_out_12));
  Multiplexer #(.select(3)) multiplexer_1 (
    .in0(n4_bit_adder_1_sum0), .in1(adder_subtractor_1_sum0), .in2(adder_subtractor_2_sum0),
    .in3(n4_bit_adder_2_sum0), .in4(n4_bit_and_1_out_9), .in5(n4_bit_or_1_out_9), .in6(n4_bit_not_1_out_5),
    .in7(n4_bit_xor_1_out_9), .out(OUT0), .sel(Selector));  // open: en
  Multiplexer #(.select(3)) multiplexer_2 (
    .in0(n4_bit_adder_1_sum1), .in1(adder_subtractor_1_sum1), .in2(adder_subtractor_2_sum1),
    .in3(n4_bit_adder_2_sum1), .in4(n4_bit_and_1_out_10), .in5(n4_bit_or_1_out_10), .in6(n4_bit_not_1_out_6),
    .in7(n4_bit_xor_1_out_10), .out(OUT1), .sel(Selector));  // open: en
  Multiplexer #(.select(3)) multiplexer_3 (
    .in0(n4_bit_adder_1_sum2), .in1(adder_subtractor_1_sum2), .in2(adder_subtractor_2_sum2),
    .in3(n4_bit_adder_2_sum2), .in4(n4_bit_and_1_out_11), .in5(n4_bit_or_1_out_11), .in6(n4_bit_not_1_out_7),
    .in7(n4_bit_xor_1_out_11), .out(OUT2), .sel(Selector));  // open: en
  Multiplexer #(.select(3)) multiplexer_4 (
    .in0(n4_bit_adder_1_sum3), .in1(adder_subtractor_1_sum3), .in2(adder_subtractor_2_sum3),
    .in3(n4_bit_adder_2_sum3), .in4(n4_bit_and_1_out_12), .in5(n4_bit_or_1_out_12), .in6(n4_bit_not_1_out_8),
    .in7(n4_bit_xor_1_out_12), .out(OUT3), .sel(Selector));  // open: en
  Multiplexer #(.select(3)) multiplexer_5 (
    .in0(n4_bit_adder_1_carry), .in1(adder_subtractor_1_carry), .in2(adder_subtractor_2_carry),
    .in3(n4_bit_adder_2_carry), .in4(1'b0), .in5(1'b0), .in6(1'b0), .in7(1'b0), .out(Carry), .sel(Selector));  // open: en
endmodule

module TEST (
  input  in_1,
  input  in_2,
  input  in_3,
  input  in_4,
  input  in_5,
  input  in_6,
  input  [2:0] in_7,
  input  in_8,
  input  in_9,
  output out_10,
  output out_11,
  output out_12,
  output out_13,
  output out_14
);

  ALU alu_1 (
    .A0(in_1), .A1(in_2), .A2(in_3), .A3(in_4), .B0(in_5), .B1(in_6), .B2(in_8), .B3(in_9), .OUT0(out_10),
    .OUT1(out_11), .OUT2(out_12), .OUT3(out_13), .Carry(out_14), .Selector(in_7));
  Hex_Digit_Display hex_digit_display_1 (.value({out_13, out_12, out_11, out_10}));  // open: dp
endmodule
